# Fritzing sketch serial-plotter (saved by Fritzing 0.9.3b)
breadboards: 1

parts:
  Part1 = Arduino Uno (Rev3) - ICSP
  R1 = PHOTOCELL [package=photocell]
  R2 = Resistor [tolerance=±5% resistance=10k package=THT]
  U1 = SLIDER [package=slider]

nets:
  N1: Part1.A3, R1.P$1, R2.Pin_0
  N2: Part1.A5/SCL, U1.S
  N3: R1.P$2, U1.E
  N4: R2.Pin_1, U1.A
